// Logisim project decoders.circ as structural Verilog: 1 circuit, main circuit main
module main (
  input  A,
  input  B,
  input  in_3,
  output out_4,
  output out_5,
  output out_6,
  output out_7
);

  wire not_1_out, not_2_out;

  not not_1 (not_1_out, B);
  not not_2 (not_2_out, in_3);
  and and_1 (out_4, not_1_out, A, not_2_out);
  and and_2 (out_5, not_1_out, A, in_3);
  and and_3 (out_6, B, A, not_2_out);
  and and_4 (out_7, B, A, in_3);
endmodule
